# Fritzing sketch Motorized Focuser (saved by Fritzing 0.9.3b)
breadboards: 1

parts:
  Arduino_UNO_Board = Arduino Uno (Rev3)
  S1 = SWITCH-MOMENTARY-2 [package=tactile-pth]
  S2 = SWITCH-MOMENTARY-2 [package=tactile-pth]
  S3 = SWITCH-MOMENTARY-2 [package=tactile-pth]
  S4 = SWITCH-MOMENTARY-2 [package=tactile-pth]
  10k = Resistor [tolerance=±5% resistance=220 package="2010 [SMD]"]
  10k_2 = Resistor [tolerance=±5% resistance=220 package="2010 [SMD]"]
  10k_3 = Resistor [tolerance=±5% resistance=220 package="2010 [SMD]"]
  10k_4 = Resistor [tolerance=±5% resistance=220 package="2010 [SMD]"]
  10k_5 = Resistor [tolerance=±5% resistance=220 package="2010 [SMD]"]
  10k_6 = Resistor [tolerance=±5% resistance=220 package="2010 [SMD]"]
  Joystick_SMD_tactile = JOYSTICK_MINI [package=joystick_mini]
  10nF = Capacitor [package=cap-pth-5mm]
  10nF_2 = Capacitor [package=cap-pth-5mm]
  10nF_3 = Capacitor [package=cap-pth-5mm]
  10nF_4 = Capacitor [package=cap-pth-5mm]
  10nF_5 = Capacitor [package=cap-pth-5mm]
  10nF_6 = Capacitor [package=cap-pth-5mm]
  10nF_7 = Capacitor [package=cap-pth-5mm]
  Arduino_12v_In = Power Jack [package=power_jack_slot]
  10K = Resistor [tolerance=±5% resistance=220 package="2010 [SMD]"]
  Motor_Driver = Pololu A4988 [package=SO16]
  42SHDC3025-24B = Stepper Motor - Bipolar

nets:
  N1: Arduino_UNO_Board.A0, Motor_Driver.MS1
  N2: Arduino_UNO_Board.A1, Motor_Driver.MS2
  N3: Arduino_UNO_Board.A2, Motor_Driver.MS3
  N4: Arduino_UNO_Board.D8, S4.2, 10nF_4.2
  N5: Arduino_UNO_Board.D9_PWM, 10k_3.Pin_0
  N6: Arduino_UNO_Board.D10_PWM/SS, 10k_2.Pin_0
  N7: Arduino_UNO_Board.D11_PWM/MOSI, S1.2, 10nF.2
  N8: Arduino_UNO_Board.D12/MISO, 10k_5.Pin_0
  N9: Arduino_UNO_Board.D13/SCK, Joystick_SMD_tactile.DOWN, 10nF_7.1, 10K.Pin_0
  GND: Arduino_UNO_Board.GND, 10k.Pin_1, 10k_2.Pin_1, 10k_3.Pin_1, 10k_4.Pin_1, 10k_5.Pin_1, 10k_6.Pin_1, 10K.Pin_1, Motor_Driver.GND#8
  N10: Arduino_UNO_Board.D3_PWM, 10k_6.Pin_0, Joystick_SMD_tactile.UP
  N11: Arduino_UNO_Board.D4, Motor_Driver.DIR
  N12: Arduino_UNO_Board.D5_PWM, Motor_Driver.STEP
  N13: Arduino_UNO_Board.D7, Motor_Driver.SLEEP
  5V: Arduino_UNO_Board.5V, S1.1, 10nF.1, Motor_Driver.RESET, Motor_Driver.VDD
  N14: S2.1, 10nF_2.1
  N15: S2.2, 10nF_2.2
  N16: S3.1, S4.1, 10nF_3.1, 10nF_4.1
  N17: S3.2, 10nF_3.2
  N18: Joystick_SMD_tactile.CENT, 10nF_5.1
  N19: Joystick_SMD_tactile.GND, 10nF_5.2, 10nF_6.2, 10nF_7.2
  N20: Arduino_12v_In.GNDBREAK, Motor_Driver.VMOT
  N21: Arduino_12v_In.PWR, Motor_Driver.GND#14
  N22: Motor_Driver.1B, 42SHDC3025-24B.C
  N23: Motor_Driver.1A, 42SHDC3025-24B.A
  N24: Motor_Driver.2A, 42SHDC3025-24B.B
  N25: Motor_Driver.2B, 42SHDC3025-24B.D
